# Fritzing sketch ESP_WITH_MIC (saved by Fritzing 0.9.3b)
circuit board: 8.46667cm x 5.64444cm
breadboards: 1

parts:
  Part1 = INMP441
  M1 = DOIT Esp32 DevKit v1 (30 pins long, 11 pins width) [part_number=ESP32S-PIN30]
  microSD1 = MicroSD Card Module

nets:
  GND: Part1.L/R, Part1.GND, M1.GND, microSD1.GND
  N1: Part1.WS, M1.D14
  N2: Part1.SCK, M1.D13
  N3: Part1.SD, M1.D34
  VDD: Part1.VDD, M1.3V3, microSD1.VCC
  N4: M1.D5, microSD1.CS
  N5: M1.D18, microSD1.SCK
  N6: M1.D19, microSD1.MISO
  N7: M1.D23, microSD1.MOSI

custom parts:
  INMP441: This is a simple breakout board for the INMP441 I2S MEMS microphone.
  DOIT Esp32 DevKit v1 (30 pins long, 11 pins width): The DOIT Esp32 DevKit v1 is one of the development board created by DOIT to evaluate the ESP-WROOM-32 module. It is based on the ESP32 microcontroller that boasts Wifi, Bluetooth, Ethernet and Low Power support all in a single chip. (vanepp) made breadboard work, adjusted pin numbering and labels and reduced size of schematic and cleaned up pcb. This chip is 30pins long (2 x15) and 11 pins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
